# Fritzing sketch Project01 (saved by Fritzing 0.9.3b)

parts:
  Componente1 = Arduino Uno (Rev3) - ICSP
  S1 = H-Bridge with L298N
  VCC1 = Battery block 9V
  M1 = DC Motor
  M2 = DC Motor
  Componente3 = Bluetooth HC-05 Macho
  Componente4 = Arduino Uno (Rev3) - ICSP
  S2 = H-Bridge with L298N
  VCC2 = Battery block 9V
  M3 = DC Motor
  M4 = DC Motor

nets:
  N1: Componente1.D8, S1.IN1
  N2: Componente1.D2, S1.IN4
  N3: Componente1.D4, S1.IN3
  N4: Componente1.D7, S1.IN2
  GND: Componente1.GND, S1.GND, VCC1.-
  VIN: Componente1.VIN, S1.5V
  N5: S1.12V, VCC1.+
  N6: S1.OUT3-Motor2, M1.pin_2
  N7: S1.OUT4-Motor2, M1.pin_1
  N8: S1.OUT1-Motor1, M2.pin_1
  N9: S1.OUT2-Motor1, M2.pin_2
  N10: Componente3.TXD, Componente4.D0/RX
  N11: Componente3.RXD, Componente4.D1/TX
  VCC: Componente3.VCC, Componente4.5V
  GND_2: Componente3.GND, Componente4.GND, S2.GND, VCC2.-
  N12: Componente4.D8, S2.IN1
  N13: Componente4.D2, S2.IN4
  N14: Componente4.D4, S2.IN3
  N15: Componente4.D7, S2.IN2
  VIN_2: Componente4.VIN, S2.5V
  N16: S2.12V, VCC2.+
  N17: S2.OUT3-Motor2, M3.pin_2
  N18: S2.OUT4-Motor2, M3.pin_1
  N19: S2.OUT1-Motor1, M4.pin_1
  N20: S2.OUT2-Motor1, M4.pin_2

custom parts:
  H-Bridge with L298N: h-bridge

// code stored in the sketch: code_arduino.ino

/**
   Software: Projeto 01
   Description: Controlando Carrrinho Arduino com App Android via Bluetooth
   Author: RodriguesFAS[
   Email: <franciscosouzaacer@gmail.com>
   Site: <http://rodrihuesfas.com.br> | <http://clubedosgeeks.com.br>
   Github: <>
   Date: 17/02/2018
   Version: 0.0.1
   Atencion: Before transferring the code to the Arduino board, remove the Bluetooth TX or RX pins from the Arduino board, otherwise the transfer will fail.
*/

// Custom Util
#include <BUMBLEBEE.h>

/**
  Instantiate an object of class BUMBLEBEE, passing parameters the connecting pins
  where this on each pin of the H bridge L298N in Arduino doors.
*/
#define PIN1_MOTOR_LEFT           2
#define PIN2_MOTOR_LEFT           4
#define PIN_PWM_SPEED_MOTOR_LEFT  3

#define PIN1_MOTOR_RIGHT          6
#define PIN2_MOTOR_RIGHT          7
#define PIN_PWM_SPEED_MOTOR_RIGHT 5

BUMBLEBEE bee(PIN1_MOTOR_LEFT, PIN2_MOTOR_LEFT, PIN_PWM_SPEED_MOTOR_LEFT, PIN1_MOTOR_RIGHT, PIN2_MOTOR_RIGHT, PIN_PWM_SPEED_MOTOR_RIGHT);

#define SPEED 200
#define SPEED_AUX 55


#define BUZZER 13


/**
  ========================================================================================================================
  setup - configuration initial.
*/
void setup() {
  Serial.begin(9600);
  pinMode(BUZZER, OUTPUT);
}

/**
  ========================================================================================================================
  loop -
*/
void loop() {

  if (Serial.available()) {
    char inByte = Serial.read();
    controlSerialBluethoot(inByte);
  }

}

/**
  ========================================================================================================================
  controlSerialBluethoot
*/
void controlSerialBluethoot(char option) {
  /**
     [S] STOP|NONE
     [F] UP
     [I] UP/RIGHT
     [R] RIGHT
     [J] DOWN/RIGHT
     [B] DOWN
     [H] DOWN/LEFT
     [L] LEFT
     [G] UP/LEFT
     [default] STOP|NONE
  */
  switch (option) {

    case 'S':
      bee.stop();
      break;

    case 'F':
      bee.move(SPEED, SPEED);
      break;

    case 'I':
      bee.move(SPEED + SPEED_AUX, SPEED);
      break;

    case 'R':
      bee.move(SPEED, -SPEED);
      break;

    case 'J':
      bee.move(-SPEED + SPEED_AUX, -SPEED);
      break;

    case 'B':
      bee.move(-SPEED, -SPEED);
      break;

    case 'H':
      bee.move(-SPEED, -SPEED + SPEED_AUX);
      break;

    case 'L':
      bee.move(-SPEED, SPEED);
      break;

    case 'G':
      bee.move(-SPEED, SPEED + SPEED_AUX);
      break;

    default :
      bee.stop();
      break;
  }

  // Buzzer
  if (option == 'V') {
    tone(BUZZER, 1000);
  } else if (option == 'v') {
    noTone(BUZZER);
  }

}
